// Logisim project Design with additional Functionalities.circ as structural Verilog: 8 circuits, main circuit main
module main (
  input  Sensor_B,
  input  Sensor_A,
  input  EMERGENCY
);

  wire _0_out, _1_out, _2_out, _3_out, _4_out, _5_out, _6_out, _7_out, _8_out, _9_out, and_1_out, and_2_out,
       CLK_out, CLR_out, entry_detect_1_enable_for_other, entry_detect_1_output,
       exit_detect_1_enable_for_other, exit_detect_1_output, main_compare_1_out_5, multiplexer_1_out,
       not_1_out, not_2_out, OPEN_CLOSE_during_Emergency_out, or_1_out, Reset_out, xor_1_out,
       zero_compare_1_out_3;
  wire [3:0] display_1_one_s, display_1_ten_s, n2_digit_bcd_cntr_1_ones_s, n2_digit_bcd_cntr_1_ten_s;

  Button _1 (.out(_1_out));
  Button _4 (.out(_4_out));
  Button _7 (.out(_7_out));
  Hex_Digit_Display hex_digit_display_1 (.value(n2_digit_bcd_cntr_1_ten_s));  // open: dp
  Hex_Digit_Display hex_digit_display_2 (.value(display_1_ten_s));  // open: dp
  Button _2 (.out(_2_out));
  Button _3 (.out(_3_out));
  Button _6 (.out(_6_out));
  Button _5 (.out(_5_out));
  Button _9 (.out(_9_out));
  Button _8 (.out(_8_out));
  Button CLR (.out(CLR_out));
  Button _0 (.out(_0_out));
  Button OPEN_CLOSE_during_Emergency (.out(OPEN_CLOSE_during_Emergency_out));
  Hex_Digit_Display hex_digit_display_3 (.value(n2_digit_bcd_cntr_1_ones_s));  // open: dp
  Hex_Digit_Display hex_digit_display_4 (.value(display_1_one_s));  // open: dp
  Display display_1 (
    ._0(_0_out), ._1(_1_out), ._2(_2_out), ._3(_3_out), ._4(_4_out), ._5(_5_out), ._6(_6_out), ._7(_7_out),
    ._8(_8_out), ._9(_9_out), .CLR(CLR_out), .One_s(display_1_one_s), .Ten_s(display_1_ten_s));
  Button Reset (.out(Reset_out));
  Clock CLK (.out(CLK_out));
  Exit_Detect exit_detect_1 (
    .X(Sensor_A), .Output(exit_detect_1_output), .Y(Sensor_B), .CLK(CLK_out),
    .ENABLE(entry_detect_1_enable_for_other), .Enable_For_Other(exit_detect_1_enable_for_other));
  Entry_Detect entry_detect_1 (
    .ENABLE(exit_detect_1_enable_for_other), .Enable_For_Other(entry_detect_1_enable_for_other),
    .X(Sensor_A), .Output(entry_detect_1_output), .Y(Sensor_B), .CLK(CLK_out));
  or or_1 (or_1_out, Sensor_B, Sensor_A);
  and and_1 (and_1_out, exit_detect_1_output, not_1_out);
  not not_1 (not_1_out, zero_compare_1_out_3);
  and and_2 (and_2_out, entry_detect_1_output, not_2_out);
  not not_2 (not_2_out, main_compare_1_out_5);
  LED #(.active("false")) led_1 (.in(or_1_out));
  xor xor_1 (xor_1_out, and_1_out, and_2_out);
  _2_digit_BCD_cntr u_2_digit_bcd_cntr_1 (
    .SUB(and_1_out), .CNT(xor_1_out), .RESET(Reset_out), .CLK(CLK_out), .Ones_s(n2_digit_bcd_cntr_1_ones_s),
    .Ten_s(n2_digit_bcd_cntr_1_ten_s));
  Zero_Compare zero_compare_1 (
    .Current_1(n2_digit_bcd_cntr_1_ones_s), .Current_10(n2_digit_bcd_cntr_1_ten_s),
    .out_3(zero_compare_1_out_3));
  Main_Compare main_compare_1 (
    .Current_1(n2_digit_bcd_cntr_1_ones_s), .Current_10(n2_digit_bcd_cntr_1_ten_s),
    .Limit_1(display_1_one_s), .Limit_10(display_1_ten_s), .out_5(main_compare_1_out_5));
  LED #(.active("false")) led_2 (.in(multiplexer_1_out));
  Multiplexer #(.enable("false")) multiplexer_1 (
    .in0(main_compare_1_out_5), .in1(OPEN_CLOSE_during_Emergency_out), .out(multiplexer_1_out),
    .sel(EMERGENCY));

  // Notes on the sheet:
  //   Current Value
  //   Limit
  //   Detect Exit
  //   Detect Entry
  //   *please simulate the circuit by setting the clock frequency at 4.1 kHz
  //   ENTER/EXIT
  //   (* this light indicates whether the next person can enter/exit)
  //   BCD Counter
  //   Compare With 0
  //   Compare With Limit
  //   Actuator
endmodule

module Exit_Detect (
  input  X,
  input  Y,
  input  CLK,
  input  ENABLE,
  output Enable_For_Other,
  output Output
);

  wire A_prime_B_out, A_prime_B_prime_out, A_q, A_qn, and_1_out, and_2_out, and_3_out, and_4_out, B_q, B_qn,
       not_1_out, not_2_out, or_1_out, or_2_out, or_3_out, or_4_out;

  not not_1 (not_1_out, X);
  not not_2 (not_2_out, Y);
  and and_1 (and_1_out, X, or_1_out);
  or or_1 (or_1_out, Y, B_q);
  and and_2 (and_2_out, not_1_out, Y);
  or or_2 (or_2_out, and_2_out, and_3_out);
  and and_3 (and_3_out, B_q, not_2_out);
  and and_4 (and_4_out, not_1_out, or_3_out);
  or or_3 (or_3_out, A_q, Y);
  or or_4 (or_4_out, X, not_2_out);
  J_K_Flip_Flop A (.J(and_1_out), .clk(CLK), .K(or_2_out), .Q(A_q), .Qn(A_qn), .en(ENABLE));  // open: preset, reset
  J_K_Flip_Flop B (.J(and_4_out), .clk(CLK), .K(or_4_out), .Q(B_q), .Qn(B_qn), .en(ENABLE));  // open: preset, reset
  and A_prime_B_prime (A_prime_B_prime_out, A_qn, B_qn);
  and A_B (Output, A_q, B_q);
  and A_prime_B (A_prime_B_out, A_qn, B_q);
  S_R_Flip_Flop s_r_ff_1 (
    .S(A_prime_B_prime_out), .clk(CLK), .R(A_prime_B_out), .Q(Enable_For_Other));  // open: Qn, preset, reset, en

  // Notes on the sheet:
  //   Y'
  //   A
  //   X'
  //   B
  //   X'.Y + B.Y'
  //   X'.(A+Y)
  //   X+Y'
  //   X.(B+Y)
endmodule

module Entry_Detect (
  input  X,
  input  Y,
  input  CLK,
  input  ENABLE,
  output Enable_For_Other,
  output Output
);

  wire A_prime_B_out, A_prime_B_prime_out, A_q, A_qn, and_1_out, and_2_out, and_3_out, and_4_out, B_q, B_qn,
       not_1_out, not_2_out, or_1_out, or_2_out, or_3_out, or_4_out;

  not not_1 (not_1_out, X);
  not not_2 (not_2_out, Y);
  or or_1 (or_1_out, X, B_q);
  and and_1 (and_1_out, not_2_out, X);
  and and_2 (and_2_out, B_q, not_1_out);
  or or_2 (or_2_out, A_q, X);
  and and_3 (and_3_out, Y, or_1_out);
  or or_3 (or_3_out, and_1_out, and_2_out);
  and and_4 (and_4_out, not_2_out, or_2_out);
  or or_4 (or_4_out, not_1_out, Y);
  J_K_Flip_Flop A (.J(and_3_out), .clk(CLK), .K(or_3_out), .Q(A_q), .Qn(A_qn), .en(ENABLE));  // open: preset, reset
  J_K_Flip_Flop B (.J(and_4_out), .clk(CLK), .K(or_4_out), .Q(B_q), .Qn(B_qn), .en(ENABLE));  // open: preset, reset
  and A_prime_B_prime (A_prime_B_prime_out, A_qn, B_qn);
  and A_B (Output, A_q, B_q);
  and A_prime_B (A_prime_B_out, A_qn, B_q);
  S_R_Flip_Flop s_r_ff_1 (
    .S(A_prime_B_prime_out), .clk(CLK), .R(A_prime_B_out), .Q(Enable_For_Other));  // open: Qn, preset, reset, en

  // Notes on the sheet:
  //   X'
  //   Y'
  //   A
  //   B
  //   Y.(B+X)
  //   Y'.X + B.X'
  //   Y'.(A+X)
  //   X'+Y
endmodule

module Detect_1_0 (
  input  X,
  input  CLK,
  output out_3
);

  wire A_q, and_1_out, and_2_out, B_q, nand_1_out, not_1_out, not_2_out, not_3_out;

  not not_1 (not_1_out, A_q);
  and and_1 (and_1_out, not_1_out, B_q, not_2_out);
  not not_2 (not_2_out, X);
  nand nand_1 (nand_1_out, A_q, B_q);
  and and_2 (and_2_out, nand_1_out, X);
  D_Flip_Flop A (.clk(CLK), .D(and_1_out), .Q(A_q));  // open: Qn, preset, en, reset
  D_Flip_Flop B (.clk(CLK), .D(and_2_out), .Q(B_q));  // open: Qn, preset, en, reset
  not not_3 (not_3_out, B_q);
  and and_3 (out_3, A_q, not_3_out);

  // Notes on the sheet:
  //   A
  //   B
  //   A'Bx'
  //   x(A' + B')
  //   A B'
endmodule

module _2_digit_BCD_cntr (
  input  SUB,
  input  CNT,
  input  RESET,
  input  CLK,
  output [3:0] Ones_s,
  output [3:0] Ten_s
);

  wire and_1_out, d_ff_1_q, detect_1_0_1_out_3, detect_1_0_2_out_3, detect_1_0_3_out_3, multiplexer_1_out,
       not_1_out, not_2_out;

  Counter #(.width(4), .max('h9), .trigger("falling")) counter_1 (
    .load(SUB), .count(CNT), .Q(Ones_s), .clk(CLK), .clr(RESET));  // open: D, carry
  not not_1 (not_1_out, Ones_s[3]);
  not not_2 (not_2_out, Ones_s[0]);
  D_Flip_Flop d_ff_1 (.clk(CLK), .D(SUB), .Q(d_ff_1_q));  // open: Qn, preset, en, reset
  Detect_1_0 detect_1_0_1 (.X(Ones_s[3]), .CLK(CLK), .out_3(detect_1_0_1_out_3));
  Detect_1_0 detect_1_0_2 (.X(not_1_out), .CLK(CLK), .out_3(detect_1_0_2_out_3));
  Detect_1_0 detect_1_0_3 (.X(not_2_out), .CLK(CLK), .out_3(detect_1_0_3_out_3));
  and and_1 (and_1_out, detect_1_0_2_out_3, detect_1_0_3_out_3);
  Counter #(.width(4), .max('h9), .trigger("falling")) counter_2 (
    .load(d_ff_1_q), .D(Ten_s), .count(multiplexer_1_out), .Q(Ten_s), .clk(CLK), .clr(RESET));  // open: carry
  Multiplexer #(.enable("false")) multiplexer_1 (
    .in0(detect_1_0_1_out_3), .in1(and_1_out), .out(multiplexer_1_out), .sel(d_ff_1_q));
endmodule

module Main_Compare (
  input  [3:0] Current_1,
  input  [3:0] Current_10,
  input  [3:0] Limit_1,
  input  [3:0] Limit_10,
  output out_5
);

  wire comparator_1_eq, comparator_1_gt, comparator_2_eq, comparator_2_gt, or_1_out, or_2_out;

  or or_1 (or_1_out, comparator_1_gt, comparator_1_eq);
  Comparator #(.width(4), .mode("unsigned")) comparator_1 (
    .a(Current_1), .b(Limit_1), .gt(comparator_1_gt), .eq(comparator_1_eq));  // open: lt
  or or_2 (or_2_out, comparator_2_gt, comparator_2_eq);
  Comparator #(.width(4), .mode("unsigned")) comparator_2 (
    .a(Current_10), .b(Limit_10), .gt(comparator_2_gt), .eq(comparator_2_eq));  // open: lt
  and and_1 (out_5, or_1_out, or_2_out);
endmodule

module Zero_Compare (
  input  [3:0] Current_1,
  input  [3:0] Current_10,
  output out_3
);

  wire comparator_1_eq, comparator_2_eq;

  Comparator #(.width(4), .mode("unsigned")) comparator_1 (
    .a(Current_1), .b(4'b0000), .eq(comparator_1_eq));  // open: gt, lt
  Comparator #(.width(4), .mode("unsigned")) comparator_2 (
    .a(Current_10), .b(4'b0000), .eq(comparator_2_eq));  // open: gt, lt
  and and_1 (out_3, comparator_1_eq, comparator_2_eq);
endmodule

module Display (
  input  _0,
  input  _1,
  input  _2,
  input  _3,
  input  _4,
  input  _5,
  input  _6,
  input  _7,
  input  _8,
  input  _9,
  input  CLR,
  output [3:0] Ten_s,
  output [3:0] One_s
);

  wire nor_1_out, priority_encoder_1_gs;
  wire [3:0] priority_encoder_1_out;

  Priority_Encoder #(.select(4)) priority_encoder_1 (
    .in0(_0), .in1(_1), .in2(_2), .in3(_3), .in4(_4), .in5(_5), .in6(_6), .in7(_7), .in8(_8), .in9(_9),
    .in10(1'b0), .in11(1'b0), .in12(1'b0), .in13(1'b0), .in14(1'b0), .in15(1'b0),
    .out(priority_encoder_1_out), .gs(priority_encoder_1_gs));  // open: en_out, en_in
  Register #(.width(4)) register_1 (
    .D(priority_encoder_1_out), .en(nor_1_out), .Q(One_s), .clk(priority_encoder_1_gs), .clr(CLR));
  Register #(.width(4)) register_2 (.D(One_s), .en(nor_1_out), .Q(Ten_s), .clk(priority_encoder_1_gs), .clr(CLR));
  nor nor_1 (nor_1_out, Ten_s[0], Ten_s[1], Ten_s[2], Ten_s[3]);
endmodule
