// Logisim project Main Design.circ as structural Verilog: 7 circuits, main circuit main
module main (
  input  Sensor_B,
  input  Sensor_A
);

  wire and_1_out, and_2_out, CLK_out, entry_detect_1_output, exit_detect_1_output, main_compare_1_out_5,
       not_1_out, not_2_out, Reset_out, xor_1_out, zero_compare_1_out_3;
  wire [3:0] n2_digit_bcd_cntr_1_ones_s, n2_digit_bcd_cntr_1_ten_s;

  Hex_Digit_Display hex_digit_display_1 (.value(n2_digit_bcd_cntr_1_ten_s));  // open: dp
  Hex_Digit_Display hex_digit_display_2 (.value(4'b0001));  // open: dp
  Clock CLK (.out(CLK_out));
  Button Reset (.out(Reset_out));
  Hex_Digit_Display hex_digit_display_3 (.value(n2_digit_bcd_cntr_1_ones_s));  // open: dp
  Hex_Digit_Display hex_digit_display_4 (.value(4'b0010));  // open: dp
  Exit_Detect exit_detect_1 (.X(Sensor_A), .Y(Sensor_B), .Output(exit_detect_1_output), .CLK(CLK_out));
  Entry_Detect entry_detect_1 (.X(Sensor_A), .Output(entry_detect_1_output), .Y(Sensor_B), .CLK(CLK_out));
  and and_1 (and_1_out, exit_detect_1_output, not_1_out);
  not not_1 (not_1_out, zero_compare_1_out_3);
  and and_2 (and_2_out, entry_detect_1_output, not_2_out);
  not not_2 (not_2_out, main_compare_1_out_5);
  xor xor_1 (xor_1_out, and_1_out, and_2_out);
  _2_digit_BCD_cntr u_2_digit_bcd_cntr_1 (
    .SUB(and_1_out), .CNT(xor_1_out), .RESET(Reset_out), .CLK(CLK_out), .Ones_s(n2_digit_bcd_cntr_1_ones_s),
    .Ten_s(n2_digit_bcd_cntr_1_ten_s));
  Zero_Compare zero_compare_1 (
    .Current_1(n2_digit_bcd_cntr_1_ones_s), .Current_10(n2_digit_bcd_cntr_1_ten_s),
    .out_3(zero_compare_1_out_3));
  Main_Compare main_compare_1 (
    .Current_1(n2_digit_bcd_cntr_1_ones_s), .Current_10(n2_digit_bcd_cntr_1_ten_s), .Limit_1(4'b0010),
    .Limit_10(4'b0001), .out_5(main_compare_1_out_5));
  LED #(.active("false")) led_1 (.in(main_compare_1_out_5));

  // Notes on the sheet:
  //   Current Value
  //   Limit
  //   *please simulate the circuit by setting the clock frequency at 4.1 kHz
  //   Detect Exit
  //   Detect Entry
  //   BCD Counter
  //   Actuator
  //   Compare With 0
  //   Compare With Limit
endmodule

module Exit_Detect (
  input  X,
  input  Y,
  input  CLK,
  output Output
);

  wire A_q, and_1_out, and_2_out, and_3_out, and_4_out, B_q, not_1_out, not_2_out, or_1_out, or_2_out,
       or_3_out, or_4_out;

  not not_1 (not_1_out, X);
  not not_2 (not_2_out, Y);
  or or_1 (or_1_out, Y, B_q);
  and and_1 (and_1_out, not_1_out, Y);
  and and_2 (and_2_out, B_q, not_2_out);
  or or_2 (or_2_out, A_q, Y);
  and and_3 (and_3_out, X, or_1_out);
  or or_3 (or_3_out, and_1_out, and_2_out);
  and and_4 (and_4_out, not_1_out, or_2_out);
  or or_4 (or_4_out, X, not_2_out);
  J_K_Flip_Flop A (.J(and_3_out), .clk(CLK), .K(or_3_out), .Q(A_q));  // open: Qn, preset, en, reset
  J_K_Flip_Flop B (.J(and_4_out), .clk(CLK), .K(or_4_out), .Q(B_q));  // open: Qn, preset, en, reset
  and A_B (Output, A_q, B_q);

  // Notes on the sheet:
  //   Y'
  //   A
  //   X'
  //   B
  //   X'.Y + B.Y'
  //   X'.(A+Y)
  //   X+Y'
  //   X.(B+Y)
endmodule

module Entry_Detect (
  input  X,
  input  Y,
  input  CLK,
  output Output
);

  wire A_q, and_1_out, and_2_out, and_3_out, and_4_out, B_q, not_1_out, not_2_out, or_1_out, or_2_out,
       or_3_out, or_4_out;

  not not_1 (not_1_out, X);
  not not_2 (not_2_out, Y);
  or or_1 (or_1_out, X, B_q);
  and and_1 (and_1_out, not_2_out, X);
  and and_2 (and_2_out, B_q, not_1_out);
  or or_2 (or_2_out, A_q, X);
  and and_3 (and_3_out, Y, or_1_out);
  or or_3 (or_3_out, and_1_out, and_2_out);
  and and_4 (and_4_out, not_2_out, or_2_out);
  or or_4 (or_4_out, not_1_out, Y);
  J_K_Flip_Flop A (.J(and_3_out), .clk(CLK), .K(or_3_out), .Q(A_q));  // open: Qn, preset, en, reset
  J_K_Flip_Flop B (.J(and_4_out), .clk(CLK), .K(or_4_out), .Q(B_q));  // open: Qn, preset, en, reset
  and A_B (Output, A_q, B_q);

  // Notes on the sheet:
  //   X'
  //   Y'
  //   A
  //   B
  //   Y'.X + B.X'
  //   Y'.(A+X)
  //   X'+Y
  //   Y.(B+X)
endmodule

module Detect_1_0 (
  input  X,
  input  CLK,
  output out_3
);

  wire A_q, and_1_out, and_2_out, B_q, nand_1_out, not_1_out, not_2_out, not_3_out;

  not not_1 (not_1_out, A_q);
  and and_1 (and_1_out, not_1_out, B_q, not_2_out);
  not not_2 (not_2_out, X);
  nand nand_1 (nand_1_out, A_q, B_q);
  and and_2 (and_2_out, nand_1_out, X);
  D_Flip_Flop A (.clk(CLK), .D(and_1_out), .Q(A_q));  // open: Qn, preset, en, reset
  D_Flip_Flop B (.clk(CLK), .D(and_2_out), .Q(B_q));  // open: Qn, preset, en, reset
  not not_3 (not_3_out, B_q);
  and and_3 (out_3, A_q, not_3_out);

  // Notes on the sheet:
  //   A
  //   B
  //   A'Bx'
  //   x(A' + B')
  //   A B'
endmodule

module _2_digit_BCD_cntr (
  input  SUB,
  input  CNT,
  input  RESET,
  input  CLK,
  output [3:0] Ones_s,
  output [3:0] Ten_s
);

  wire and_1_out, d_ff_1_q, detect_1_0_1_out_3, detect_1_0_2_out_3, detect_1_0_3_out_3, multiplexer_1_out,
       not_1_out, not_2_out;

  Counter #(.width(4), .max('h9), .trigger("falling")) counter_1 (
    .load(SUB), .count(CNT), .Q(Ones_s), .clk(CLK), .clr(RESET));  // open: D, carry
  not not_1 (not_1_out, Ones_s[3]);
  not not_2 (not_2_out, Ones_s[0]);
  D_Flip_Flop d_ff_1 (.clk(CLK), .D(SUB), .Q(d_ff_1_q));  // open: Qn, preset, en, reset
  Detect_1_0 detect_1_0_1 (.X(Ones_s[3]), .CLK(CLK), .out_3(detect_1_0_1_out_3));
  Detect_1_0 detect_1_0_2 (.X(not_1_out), .CLK(CLK), .out_3(detect_1_0_2_out_3));
  Detect_1_0 detect_1_0_3 (.X(not_2_out), .CLK(CLK), .out_3(detect_1_0_3_out_3));
  and and_1 (and_1_out, detect_1_0_2_out_3, detect_1_0_3_out_3);
  Counter #(.width(4), .max('h9), .trigger("falling")) counter_2 (
    .load(d_ff_1_q), .D(Ten_s), .count(multiplexer_1_out), .Q(Ten_s), .clk(CLK), .clr(RESET));  // open: carry
  Multiplexer #(.enable("false")) multiplexer_1 (
    .in0(detect_1_0_1_out_3), .in1(and_1_out), .out(multiplexer_1_out), .sel(d_ff_1_q));
endmodule

module Main_Compare (
  input  [3:0] Current_1,
  input  [3:0] Current_10,
  input  [3:0] Limit_1,
  input  [3:0] Limit_10,
  output out_5
);

  wire comparator_1_eq, comparator_1_gt, comparator_2_eq, comparator_2_gt, or_1_out, or_2_out;

  or or_1 (or_1_out, comparator_1_gt, comparator_1_eq);
  Comparator #(.width(4), .mode("unsigned")) comparator_1 (
    .a(Current_1), .b(Limit_1), .gt(comparator_1_gt), .eq(comparator_1_eq));  // open: lt
  or or_2 (or_2_out, comparator_2_gt, comparator_2_eq);
  Comparator #(.width(4), .mode("unsigned")) comparator_2 (
    .a(Current_10), .b(Limit_10), .gt(comparator_2_gt), .eq(comparator_2_eq));  // open: lt
  and and_1 (out_5, or_1_out, or_2_out);
endmodule

module Zero_Compare (
  input  [3:0] Current_1,
  input  [3:0] Current_10,
  output out_3
);

  wire comparator_1_eq, comparator_2_eq;

  Comparator #(.width(4), .mode("unsigned")) comparator_1 (
    .a(Current_1), .b(4'b0000), .eq(comparator_1_eq));  // open: gt, lt
  Comparator #(.width(4), .mode("unsigned")) comparator_2 (
    .a(Current_10), .b(4'b0000), .eq(comparator_2_eq));  // open: gt, lt
  and and_1 (out_3, comparator_1_eq, comparator_2_eq);
endmodule
